# Fritzing sketch EasyPicoPCB_fritzing (saved by Fritzing 1.0.1rc)
circuit board: 9cm x 9cm
breadboards: 1

parts:
  R1 = Resistor [tolerance=±5% power=0.25 resistance=47 package=THT]
  P3 = Trimmer Potentiometer [maximum_resistance=10kΩ knob_status=50% power=0.5W package=THT]
  P2 = Trimmer Potentiometer [maximum_resistance=10kΩ knob_status=50% power=0.5W package=THT]
  P1 = Trimmer Potentiometer [maximum_resistance=10kΩ knob_status=50% power=0.5W package=THT]
  R2 = Resistor [tolerance=±5% power=0.25 resistance=68 package=THT]
  LED2 = LED - 3mm [color="Orange (620nm)" current=20mA package="3 mm [THT]"]
  LED3 = LED - 3mm [color="Red (660nm)" current=20mA package="3 mm [THT]"]
  R3 = Resistor [tolerance=±5% power=0.25 resistance=100 package=THT]
  J3 = female pin header, 20 pins [form="♀ (female)"]
  J4 = female pin header, 20 pins [form="♀ (female)"]
  J2 = female pin header, 20 pins [form="♀ (female)"]
  J1 = female pin header, 20 pins [form="♀ (female)"]
  LED1 = LED - 3mm [color="Green (565nm)" current=20mA package="3 mm [THT]"]
  S1 = Momentary Switch [package=ksa_sealed_tac_switch]
  S2 = Momentary Switch [package=ksa_sealed_tac_switch]
  S3 = Momentary Switch [package=ksa_sealed_tac_switch]
  Raspberry_Pi_Pico = Raspberry Pi Pico  # not connected

nets:
  GND: R1.Pin_0, P3.leg2, P2.leg2, P1.leg2, R2.Pin_0, R3.Pin_0, J3.pin18, J4.pin18, J2.pin18, J1.pin18
  N1: R1.Pin_1, LED1.anode
  N2: P3.leg1, P2.leg1, P1.leg1, J3.pin5, J4.pin5, S1.1, S2.1, S3.1
  N3: P3.wiper, J3.pin7, J4.pin7
  N4: P2.wiper, J3.pin9, J4.pin9
  N5: P1.wiper, J3.pin10, J4.pin10
  N6: R2.Pin_1, LED2.anode
  N7: LED2.cathode, J2.pin19, J1.pin19
  N8: LED3.cathode, J2.pin17, J1.pin17
  N9: LED3.anode, R3.Pin_1
  N10: J3.pin1, J4.pin1
  N11: J3.pin2, J4.pin2
  N12: J3.pin3, J4.pin3
  N13: J3.pin4, J4.pin4
  N14: J3.pin6, J4.pin6
  N15: J3.pin8, J4.pin8
  N16: J3.pin11, J4.pin11
  N17: J3.pin12, J4.pin12
  N18: J3.pin13, J4.pin13
  N19: J3.pin14, J4.pin14
  N20: J3.pin15, J4.pin15
  N21: J3.pin16, J4.pin16
  N22: J3.pin17, J4.pin17, S3.3
  N23: J3.pin19, J4.pin19, S2.3
  N24: J3.pin20, J4.pin20, S1.3
  N25: J2.pin1, J1.pin1
  N26: J2.pin2, J1.pin2
  N27: J2.pin3, J1.pin3
  N28: J2.pin4, J1.pin4
  N29: J2.pin5, J1.pin5
  N30: J2.pin6, J1.pin6
  N31: J2.pin7, J1.pin7
  N32: J2.pin8, J1.pin8
  N33: J2.pin9, J1.pin9
  N34: J2.pin10, J1.pin10
  N35: J2.pin11, J1.pin11
  N36: J2.pin12, J1.pin12
  N37: J2.pin13, J1.pin13
  N38: J2.pin14, J1.pin14
  N39: J2.pin15, J1.pin15
  N40: J2.pin16, J1.pin16
  N41: J2.pin20, J1.pin20, LED1.cathode

notes:
  EasyPicoPCB
  EasyPicoPCB(2023-10-06)
  Made with fritzing
  USB
  ! 3,3V from the Pico !
  R (Ohm) = (Vcc - Vf) / I (Amp)
  Green LED : 45  = (3,3 - 2,4) / 0.02
  Orange LED : 65  = (3,3 - 2) / 0.02
  Red LED : 85  = (3,3 - 1,6) / 0.02
  3.3v
  (2023-10-06)

custom parts:
  Raspberry Pi Pico: Raspberry Pi Pico. Based around the RP2040 microcontroller the Pico is a low cost microcontroller device bringing Raspberry Pi quality, cost, and easy of use to the microcontroller space. Jan 2021, Split part in to two versions: tht (this one) and SMD. This one will drill holes for a .1 in header in pcb to allow plugging in the module as well as providing pads to solder the module to the top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

// code stored in the sketch: EasyPicoPCB.ino

